// Digital circuit 74HCT258.dig as structural Verilog
module _74HCT258 (
  input  [3:0] A,
  input  [3:0] B,
  input  SEL_B,
  input  ENABLE,
  output [3:0] Y
);

  wire _74157_1_pin15;
  wire [3:0] _74157_1_pin4;

  _74157 _74157_1 (
    .pin1(SEL_B), .pin2(A[0]), .pin3(B[0]), .pin4(_74157_1_pin4[0]), .pin5(A[1]), .pin6(B[1]),
    .pin7(_74157_1_pin4[1]), .pin8(1'b0), .pin9(_74157_1_pin4[2]), .pin10(B[2]), .pin11(A[2]),
    .pin12(_74157_1_pin4[3]), .pin13(B[3]), .pin14(A[3]), .pin15(_74157_1_pin15), .pin16(1'b1));
  not not_1 (_74157_1_pin15, ENABLE);
  assign Y = ENABLE ? _74157_1_pin4 : 4'bz;  // Driver driver_1
endmodule
