// Digital circuit ALU.dig as structural Verilog
module ALU (
  input  [3:0] IN,
  input  LD_A,
  input  CLK_LD,
  input  nOE,
  input  C_IN,
  input  nAOE,
  input  nBOE,
  input  S0,
  input  S1,
  input  S2,
  input  [1:0] SEL_BIT,
  input  SEL_A,
  input  BIT,
  output C,
  output Z,
  output [3:0] OUT,
  output OVR,
  output COND
);

  wire _74253_1_pin7, _74253_1_pin9, _74253_1_pin15, _74382_1_pin2, _74382_1_pin4, _74382_1_pin8,
       _74382_1_pin9, _74382_1_pin11, _74382_1_pin12, _74382_1_pin16, _74382_1_pin18, A_pin11, and_2_out,
       not_2_out, or_1_out;
  wire [3:0] _74253_1_pin6, _74253_1_pin13;

  _74253 _74253_1 (
    .pin1(SEL_A), .pin2(SEL_BIT[1]), .pin3(_74253_1_pin6[3]), .pin4(_74253_1_pin6[2]),
    .pin5(_74253_1_pin6[1]), .pin6(_74253_1_pin6[0]), .pin7(_74253_1_pin7), .pin8(1'b0),
    .pin9(_74253_1_pin9), .pin10(_74253_1_pin13[0]), .pin11(_74253_1_pin13[1]), .pin12(_74253_1_pin13[2]),
    .pin13(_74253_1_pin13[3]), .pin14(SEL_BIT[0]), .pin15(_74253_1_pin15), .pin16(1'b1));
  not not_1 (_74253_1_pin15, SEL_A);
  _74574 A (
    .pin1(nAOE), .pin2(IN[0]), .pin3(IN[1]), .pin4(IN[2]), .pin5(IN[3]), .pin6(1'b0), .pin7(1'b0),
    .pin8(1'b0), .pin9(1'b0), .pin10(1'b0), .pin11(A_pin11), .pin16(_74253_1_pin13[3]),
    .pin17(_74253_1_pin13[2]), .pin18(_74253_1_pin13[1]), .pin19(_74253_1_pin13[0]), .pin20(1'b1));  // open: pin12, pin13, pin14, pin15
  and and_1 (A_pin11, CLK_LD, LD_A);
  not not_2 (not_2_out, LD_A);
  or or_1 (or_1_out, _74253_1_pin9, _74253_1_pin7);
  and and_2 (and_2_out, CLK_LD, not_2_out);
  // Probe A on _74253_1_pin13
  xnor xnor_1 (COND, or_1_out, BIT);
  // Probe Flags on _74253_1_pin6
  _74382 _74382_1 (
    .pin1(_74253_1_pin13[1]), .pin2(_74382_1_pin2), .pin3(_74253_1_pin13[0]), .pin4(_74382_1_pin4),
    .pin5(S0), .pin6(S1), .pin7(S2), .pin8(_74382_1_pin8), .pin9(_74382_1_pin9), .pin10(1'b0),
    .pin11(_74382_1_pin11), .pin12(_74382_1_pin12), .pin13(_74253_1_pin6[2]), .pin14(_74253_1_pin6[1]),
    .pin15(C_IN), .pin16(_74382_1_pin16), .pin17(_74253_1_pin13[3]), .pin18(_74382_1_pin18),
    .pin19(_74253_1_pin13[2]), .pin20(1'b1));
  nor nor_1 (_74253_1_pin6[0], _74382_1_pin8, _74382_1_pin9, _74382_1_pin12, _74382_1_pin11);
  _74541 BUF (
    .pin1(nOE), .pin2(_74382_1_pin8), .pin3(_74382_1_pin9), .pin4(_74382_1_pin11), .pin5(_74382_1_pin12),
    .pin6(_74253_1_pin6[0]), .pin7(_74253_1_pin6[1]), .pin8(_74253_1_pin6[2]), .pin9(_74253_1_pin6[3]),
    .pin10(_74253_1_pin6[3]), .pin12(OVR), .pin13(C), .pin14(Z), .pin15(OUT[3]), .pin16(OUT[2]),
    .pin17(OUT[1]), .pin18(OUT[0]), .pin19(1'b0), .pin20(1'b1));  // open: pin11
  _74574 B (
    .pin1(nBOE), .pin2(IN[0]), .pin3(IN[1]), .pin4(IN[2]), .pin5(IN[3]), .pin6(1'b0), .pin7(1'b0),
    .pin8(1'b0), .pin9(1'b0), .pin10(1'b0), .pin11(and_2_out), .pin16(_74382_1_pin16),
    .pin17(_74382_1_pin18), .pin18(_74382_1_pin2), .pin19(_74382_1_pin4), .pin20(1'b1));  // open: pin12, pin13, pin14, pin15
  // also tied to GND on the sheet: _74253_1_pin6[3]

  // Notes on the sheet:
  //   DEC B = AOE * ~BOE * ~C_IN * S0 * ~S1 * ~S2
  //   B = AOE * ~BOE * ~C_IN * S0 * S1 * ~S2
  //   INC B = AOE * ~BOE * C_IN * S0 * S1 * ~S2
  //   1 = AOE * BOE * C_IN * S0 * S1 * ~S2
  //   O = ~S0 * ~S1 * ~S2
  //   F = S0 * S1 * S2
  //   DEC A = ~AOE * BOE * ~C_IN * ~S0 * S1 * ~S2
  //   A = ~AOE * BOE * ~C_IN * S0 * S1 * ~S2
  //   INC A = ~AOE * BOE * C_IN * S0 * S1 * ~S2
  //   ~A = ~AOE * BOE * ~C_IN * S0 * ~S1 * ~S2
  //   -A = ~AOE * BOE * C_IN * S0 * ~S1 * ~S2
  //   ~B = AOE * ~BOE * ~C_IN * ~S0 * S1 * ~S2
  //   -B = AOE * ~BOE * C_IN * ~S0 * S1 * ~S2
  //   2x 74574 (synchro 3-state 8bit reg)
  //   1x 74382 ALU
  //   1x 74541 8bit latch
endmodule
