// Digital circuit Clock.dig as structural Verilog
module Clock (
  input  nRST,
  input  CLK,
  output CLK1,
  output CLK2,
  output CLK3,
  output CLK4
);

  wire _7474_1_pin2, _7474_1_pin5, _7474_1_pin8, _7474_1_pin9;

  _7474 _7474_1 (
    .pin1(nRST), .pin2(_7474_1_pin2), .pin3(CLK), .pin4(1'b1), .pin5(_7474_1_pin5), .pin6(_7474_1_pin2),
    .pin7(1'b0), .pin8(_7474_1_pin8), .pin9(_7474_1_pin9), .pin10(1'b1), .pin11(_7474_1_pin2),
    .pin12(_7474_1_pin8), .pin13(nRST), .pin14(1'b1));
  _7408 _7408_1 (
    .pin1(_7474_1_pin2), .pin2(_7474_1_pin8), .pin3(CLK1), .pin4(_7474_1_pin5), .pin5(_7474_1_pin8),
    .pin6(CLK2), .pin7(1'b0), .pin8(CLK3), .pin9(_7474_1_pin2), .pin10(_7474_1_pin9), .pin11(CLK4),
    .pin12(_7474_1_pin5), .pin13(_7474_1_pin9), .pin14(1'b1));
endmodule
