// Digital circuit Decoder.dig as structural Verilog
module Decoder (
  input  [7:0] INSTR,
  input  [3:0] IN_H,
  input  nOE,
  input  [3:0] IN_L,
  output [3:0] OUT_L,
  output [3:0] OUT_H,
  output nAH_BL,
  output nWR_ABHL,
  output nRD_RAM,
  output nWR_RAM,
  output nRD_ABHL,
  output nAB_HL,
  output SEL_B,
  output nWR_PC
);

  wire and_2_out, and_6_out, and_7_out, and_8_out, and_9_out, LDSTHL_nRD_AB, nI4, nI6, nI7, nJMP_instr_L_0,
       nJP_x_instr_L, nLDimm, nLDreg, nLDSTHL, nLDSTreg, nSTreg, or_1_out, or_2_out, or_3_out, or_4_out,
       or_5_out, or_6_out, or_7_out, or_8_out;
  wire [3:0] and_3_out;
  wire [3:3] and_1_out;

  nand nand_1 (nJMP_instr_L_0, nI7, INSTR[6], LDSTHL_nRD_AB, INSTR[4]);
  nand nand_2 (nJP_x_instr_L, nI7, INSTR[6], LDSTHL_nRD_AB, nI4);
  not not_1 (nI7, INSTR[7]);
  nand nand_3 (nLDSTHL, INSTR[7], INSTR[6]);
  not not_2 (nI6, INSTR[6]);
  not not_3 (LDSTHL_nRD_AB, INSTR[5]);
  not not_4 (nI4, INSTR[4]);
  and and_1 (and_1_out[3], INSTR[3], nLDSTreg);
  nand nand_4 (nLDimm, INSTR[7], nI6);
  nand nand_5 (nSTreg, nI7, INSTR[6], INSTR[5], INSTR[4]);
  nand nand_6 (nLDreg, nI7, INSTR[6], INSTR[5], nI4);
  and and_2 (and_2_out, nLDSTHL, nLDSTreg, nLDimm);
  assign and_3_out = IN_L & {4{nLDSTHL}};  // And and_3, 4 bits wide
  and and_4 (SEL_B, and_2_out, nJP_x_instr_L);
  and and_5 (nLDSTreg, nSTreg, nLDreg);
  _74HCT258 _74hct258_1 (.A({and_1_out[3], INSTR[2:0]}), .B(and_3_out), .SEL_B(SEL_B), .ENABLE(nOE), .Y(OUT_L));
  _74HCT258 _74hct258_2 (.A(IN_H), .B({and_1_out[3], INSTR[2:0]}), .SEL_B(SEL_B), .ENABLE(nOE), .Y(OUT_H));
  or or_1 (or_1_out, LDSTHL_nRD_AB, nLDSTHL);
  or or_2 (or_2_out, INSTR[5], nLDSTHL);
  or or_3 (or_3_out, nLDSTreg, INSTR[3]);
  or or_4 (or_4_out, LDSTHL_nRD_AB, nLDSTHL);
  or or_5 (or_5_out, INSTR[5], nLDSTHL);
  and and_6 (and_6_out, nSTreg, or_1_out);
  and and_7 (and_7_out, nLDreg, or_2_out);
  or or_6 (or_6_out, INSTR[4], nLDSTHL);
  or or_7 (or_7_out, nLDimm, INSTR[4]);
  or or_8 (or_8_out, nLDimm, INSTR[5]);
  and and_8 (and_8_out, nSTreg, or_4_out);
  and and_9 (and_9_out, nLDimm, nLDreg, or_5_out);
  or or_9 (nWR_RAM, and_6_out, nOE);
  or or_10 (nRD_RAM, and_7_out, nOE);
  and and_10 (nAH_BL, or_6_out, or_7_out, or_3_out);
  and and_11 (nAB_HL, nLDSTHL, nLDreg, or_8_out, nSTreg);
  and and_12 (nWR_PC, nJMP_instr_L_0, nJP_x_instr_L);
  or or_11 (nRD_ABHL, nOE, and_8_out);
  or or_12 (nWR_ABHL, nOE, and_9_out);

  // Other names for the same wires on the sheet: I3 = INSTR[3]; I4 = INSTR[4]; LDSTHL_nA_B = INSTR[4];
  //   nLDimm_AH = INSTR[4]; I5 = INSTR[5]; LDSTHL_nRD_RAM = INSTR[5]; LDSTHL_nWR_AB = INSTR[5]; nLDimm_AB = INSTR[5];
  //   I6 = INSTR[6]; I7 = INSTR[7]; LDSTHL_nWR_RAM = LDSTHL_nRD_AB; nI5 = LDSTHL_nRD_AB; nLDimm_HL = LDSTHL_nRD_AB

  // Notes on the sheet:
  //   5-JMP INSTR_L:0
  //   4-JP X:INSTR_L
  //   F..C
  //   LD/ST A/B [H:INSTR_L]
  //   B..8
  //   LD A,B,H,L imm INSTR_L
  //   7 ST A,B reg INSTR_L
  //   6-LD A,B reg INSTR_L
  //   L
  //   H
endmodule

/* Test case LDST [H:INSTR_L]:
INSTR IN_L IN_H OUT_L OUT_H ~WR_RAM ~RD_RAM ~WR_ABHL ~RD_ABHL ~AH/BL
0xF2 3 4      2 4 0 1 1 0 1
0xF2 3 0xF    2 0xF 0 1 1 0 1
0xC2 3 4      2 4 1 0 0 1 0
0xC2 3 0xF    2 0xF 1 0 0 1 0
*/

/* Test case LD,ST A,B reg INSTR_L:
INSTR OUT_L ~WR_RAM ~RD_RAM ~WR_ABHL ~RD_ABHL ~AH/BL ~AB/HL SEL_B
0x7A   2   0 1 1 0   1 0 0
0x72   2   0 1 1 0   0 0 0
0x6A   2   1 0 0 1   1 0 0
0x62   2   1 0 0 1   0 0 0
*/

/* Test case LD A,B,H,L imm:
INSTR OUT_L ~WR_RAM ~RD_RAM ~WR_ABHL ~RD_ABHL ~AH/BL ~AB/HL
0xB2   2   1 1 0 1   1 1
0xA2   2   1 1 0 1   0 1
0x92   2   1 1 0 1   1 0
0x82   2   1 1 0 1   0 0
*/

/* Test case JMP:
INSTR IN_H OUT_L OUT_H SEL_B ~WR_PC
0x5F  3 0 0xF 1 0
0x4E  3 0xE 3 0 0
*/
