// Digital circuit HL.dig as structural Verilog
module HL (
  input  [3:0] IN,
  input  SEL_H,
  input  DEC,
  input  INC,
  input  RST,
  input  OE,
  input  OE_HL,
  input  LD,
  output [3:0] OUT,
  output [7:0] OUT_HL
);

  wire _74193_2_pin4, _74193_2_pin12, _74193_2_pin13, _74193_2_pin14, and_1_out, and_2_out, and_3_out,
       nand_1_out, nand_2_out, nand_3_out, nand_4_out, nand_5_out, not_1_out;
  wire [3:0] _74193_2_pin6;
  wire [7:4] _74193_1_pin7;

  assign OUT_HL = OE_HL ? {_74193_1_pin7, _74193_2_pin6} : 8'bz;  // Driver driver_1
  _74HCT258 _74hct258_1 (.A(_74193_2_pin6), .B(_74193_1_pin7), .SEL_B(SEL_H), .ENABLE(OE), .Y(OUT));
  nand nand_1 (nand_1_out, SEL_H, DEC);
  nand nand_2 (nand_2_out, INC, SEL_H);
  and and_1 (and_1_out, _74193_2_pin12, nand_2_out);
  and and_2 (and_2_out, nand_1_out, _74193_2_pin13);
  nand nand_3 (nand_3_out, SEL_H, LD);
  and and_3 (and_3_out, SEL_H, RST);
  _74193 _74193_1 (
    .pin1(IN[1]), .pin2(_74193_1_pin7[5]), .pin3(_74193_1_pin7[4]), .pin4(and_2_out), .pin5(and_1_out),
    .pin6(_74193_1_pin7[6]), .pin7(_74193_1_pin7[7]), .pin8(1'b0), .pin9(IN[3]), .pin10(IN[2]),
    .pin11(nand_3_out), .pin14(and_3_out), .pin15(IN[0]), .pin16(1'b1));  // open: pin12, pin13
  not not_1 (not_1_out, SEL_H);
  nand nand_4 (nand_4_out, not_1_out, LD);
  nand nand_5 (nand_5_out, INC, not_1_out);
  _74193 _74193_2 (
    .pin1(IN[1]), .pin2(_74193_2_pin6[1]), .pin3(_74193_2_pin6[0]), .pin4(_74193_2_pin4), .pin5(nand_5_out),
    .pin6(_74193_2_pin6[2]), .pin7(_74193_2_pin6[3]), .pin8(1'b0), .pin9(IN[3]), .pin10(IN[2]),
    .pin11(nand_4_out), .pin12(_74193_2_pin12), .pin13(_74193_2_pin13), .pin14(_74193_2_pin14),
    .pin15(IN[0]), .pin16(1'b1));
  and and_4 (_74193_2_pin14, not_1_out, RST);
  nand nand_6 (_74193_2_pin4, not_1_out, DEC);
  // Probe on _74193_2_pin12
  // Probe on _74193_2_pin13

  // Notes on the sheet:
  //   IN: default 10
  //   OE: default 1
  //   OE_HL: default 1
  //   1x 74HCT258
  //   2x 74193
  //   2x 4x2-NAND
  //   1x 4x2-AND
  //   1x 8bit latch
  //   https://cz.farnell.com/texas-instruments/cd74hct193e/logic-sync-4bit-up-dn-cntr-16dip/dp/3119796
  //   https://www.digikey.cz/product-detail/en/texas-instruments/CD74HCT193E/296-2142-5-ND/38398
  //   DEC H
  //   INC H
  //   LD H
  //   RST H
  //   H
  //   LD L
  //   INC HL
  //   RST L
  //   DEC HL
endmodule
