// Digital circuit PC.dig as structural Verilog
module PC (
  input  [3:0] IN_L,
  input  [3:0] IN_H,
  input  nLD_L,
  input  nLD_H,
  input  CLK,
  output [7:0] ADDR
);

  wire PC_L_pin12, RESET_out;

  Button RESET (.out(RESET_out));
  _74193 PC_L (
    .pin1(IN_L[1]), .pin2(ADDR[1]), .pin3(ADDR[0]), .pin4(1'b1), .pin5(CLK), .pin6(ADDR[2]), .pin7(ADDR[3]),
    .pin8(1'b0), .pin9(IN_L[3]), .pin10(IN_L[2]), .pin11(nLD_L), .pin12(PC_L_pin12), .pin14(RESET_out),
    .pin15(IN_L[0]), .pin16(1'b1));  // open: pin13
  _74193 PC_H (
    .pin1(IN_H[1]), .pin2(ADDR[5]), .pin3(ADDR[4]), .pin4(1'b1), .pin5(PC_L_pin12), .pin6(ADDR[6]),
    .pin7(ADDR[7]), .pin8(1'b0), .pin9(IN_H[3]), .pin10(IN_H[2]), .pin11(nLD_H), .pin14(RESET_out),
    .pin15(IN_H[0]), .pin16(1'b1));  // open: pin12, pin13

  // Notes on the sheet:
  //   https://cz.farnell.com/texas-instruments/sn74hc193n/ic-counter-multiplier-divider/dp/3119814
endmodule
