// Digital circuit RAM.dig as structural Verilog
module RAM (
  input  [7:0] ADDR,
  input  CLK,
  input  OE,
  input  WE,
  output [3:0] DATA
);

  RAMSinglePort #(.AddrBits(8), .Bits(4)) RAM (.A(ADDR), .str(WE), .C(CLK), .ld(OE), .D(DATA));
endmodule
