// Digital circuit ROM.dig as structural Verilog
module ROM (
  input  [7:0] ADDR,
  input  nOE,
  output [7:0] DATA
);

  EEPROM_28c16 eeprom_28c16_1 (
    .A0(ADDR[0]), .A1(ADDR[1]), .A2(ADDR[2]), .A3(ADDR[3]), .A4(ADDR[4]), .A5(ADDR[5]), .A6(ADDR[6]),
    .A7(ADDR[7]), .A8(1'b0), .A9(1'b0), .A10(1'b0), .nCE(1'b0), .nOE(nOE), .nWE(1'b1), .VCC(1'b1),
    .GND(1'b0), .I_O0(DATA[0]), .I_O1(DATA[1]), .I_O2(DATA[2]), .I_O3(DATA[3]), .I_O4(DATA[4]),
    .I_O5(DATA[5]), .I_O6(DATA[6]), .I_O7(DATA[7]));
endmodule
